# Fritzing sketch led (saved by Fritzing 0.9.10b)
circuit board: 8.46667cm x 5.64444cm
breadboards: 1

parts:
  Arduino = Arduino Nano (Rev3.0)
  LED1 = LED - 5mm [color="Red (633nm)" current=0.030 package="5 mm [THT]"]
  R1 = Resistor [tolerance=±5% power=0.25 resistance=1000 package=THT]

nets:
  N1: Arduino.GND, R1.Pin_1
  N2: Arduino.5V, LED1.anode
  N3: LED1.cathode, R1.Pin_0
