# Fritzing sketch neopixel (saved by Fritzing 0.9.10b)
breadboards: 1

parts:
  Arduino = Arduino Nano (Rev3.0)
  NEOPIXEL2 = Neopixel Strip -- Black (30/m)

nets:
  GND: Arduino.GND, NEOPIXEL2.GND
  N1: Arduino.D2, NEOPIXEL2.Din
  5V: Arduino.5V, NEOPIXEL2.+5V

custom parts:
  Neopixel Strip -- Black (30/m): These NeoPixel strips have 30 digitally-addressable pixel LEDs per meter and are very affordable and are only 12.5 mm wide, 10 mm if you remove the strip from the casing.
