# Fritzing sketch poti2 (saved by Fritzing 0.9.10b)
breadboards: 1

parts:
  Arduino = Arduino Nano (Rev3.0)
  R1 = Rotary Potentiometer (Large) [maximum_resistance=100kΩ knob_status=50% power=0.5W package=THT]
  R2 = Resistor [tolerance=±5% power=0.25 resistance=1k package=THT]

nets:
  N1: Arduino.GND, R1.leg1
  N2: Arduino.5V, R1.leg2, R2.Pin_0
  N3: Arduino.A0, R1.wiper, R2.Pin_1
