# Fritzing sketch resistors (saved by Fritzing 0.9.10b)
breadboards: 1

parts:
  R1 = Resistor [tolerance=±5% power=0.25 resistance=1000 package=THT]
  R2 = Resistor [tolerance=±5% power=0.25 resistance=1000 package=THT]
  Arduino1 = Arduino Nano (Rev3.0)

nets:
  N1: R1.Pin_0, Arduino1.GND
  N2: R1.Pin_1, R2.Pin_0, Arduino1.A0
  N3: R2.Pin_1, Arduino1.5V
