# Fritzing sketch write (saved by Fritzing 0.9.10b)
breadboards: 1

parts:
  Arduino = Arduino Nano (Rev3.0)
  LED1 = LED - 5mm [color="Yellow (585nm)" current=0.030 package="5 mm [THT]"]
  R1 = Resistor [tolerance=±5% power=0.25 resistance=1000 package=THT]

nets:
  N1: Arduino.GND, LED1.cathode
  N2: Arduino.D2, R1.Pin_0
  N3: LED1.anode, R1.Pin_1
